# Fritzing sketch ir_tachometer (saved by Fritzing 0.9.3b)
breadboards: 1

parts:
  LM7805 = Voltage Regulator - 5V [package="TO220 [THT]"]
  C1 = Electrolytic Capacitor [capacitance=0.1mF voltage=16V package="100 mil [THT, electrolytic]"]
  Part1 = Arduino Pro Mini (5V)
  OLED_I2C1 = OLED 128x64 I2C Monochrome Display
  U1 = LM 358 Dual Op-Amp [part_number=LM358 package="SO 08 [SMD]"]
  Q1 = LTR-301 [part_number=IR package=ltr-301]
  S1 = Momentary Switch [package=ksa_sealed_tac_switch]
  S2 = Momentary Switch [package=ksa_sealed_tac_switch]
  LED1 = LED - 5mm [color="Red (633nm)" package="5 mm [THT]"]
  R1 = Resistor [tolerance=±5% resistance=1k package=THT]
  R2 = Resistor [tolerance=±5% resistance=1M package=THT]
  C2 = Ceramic Capacitor [capacitance=100nF voltage=10V part_number=4.7nF package="100 mil [THT, multilayer]"]
  R3 = Resistor [tolerance=±5% resistance=10k package=THT]
  Q2 = NPN-Transistor [part_number=BC547 package="TO92 [THT]"]
  LED2 = LED - 5mm [color="Infrared (940nm)" part_number="IR LED" package="5 mm [THT]"]
  R4 = Resistor [tolerance=±5% resistance=100 package=THT]
  R5 = Resistor [tolerance=±5% resistance=220 package=THT]

nets:
  5V: LM7805.input_voltage
  GND: LM7805.GND, C1.-, Part1.GND, OLED_I2C1.GND, U1.connector2, U1.connector3, Q1.E, S1.3, S2.3, R1.Pin_1, Q2.E
  VCC: LM7805.output_voltage, C1.+, Part1.VCC, OLED_I2C1.VDD, U1.connector7, R3.Pin_0, R4.Pin_0
  N1: Part1.A4, OLED_I2C1.SDA
  N2: Part1.A5, OLED_I2C1.SCK
  N3: Part1.A1, U1.connector0, R2.Pin_1
  N4: Part1.D9, S2.1
  N5: Part1.D8, S1.1
  N6: Part1.D7, R5.Pin_0
  N7: Part1.D6, LED1.anode
  N8: U1.connector1, R2.Pin_0, C2.1
  N9: Q1.C, R3.Pin_1
  N10: LED1.cathode, R1.Pin_0
  N11: Q2.B, R5.Pin_1
  N12: Q2.C, LED2.cathode
  N13: LED2.anode, R4.Pin_1
